// Logisim project LOGIKAGRY (1) — kopia.circ as structural Verilog: 1 circuit, main circuit main
// stan_pion
module main (
  input  sygnal_losowania,
  input  akceptuj_ruch,
  input  [11:0] pion_info_odczyt,
  input  [1:0] IN_ruch_ktorym_pionem,
  input  [1:0] IN_ktory_gracz,
  input  in_6,
  output CLK_SAVE,
  output [11:0] podglad,
  output [3:0] out_9,
  output out_10,
  output ZAPISZZ,
  output [11:0] Pion_Dane_do_zapisu
);

  wire and_2_out, and_3_out, and_4_out, and_5_out, and_6_out, and_7_out, and_8_out, and_9_out, and_10_out,
       and_11_out, and_12_out, and_13_out, and_14_out, and_15_out, and_16_out, and_17_out, and_18_out,
       bool_ruch_zapis, comparator_1_eq, comparator_2_eq, comparator_3_eq, comparator_3_lt, comparator_8_gt,
       comparator_9_lt, comparator_10_eq, comparator_10_gt, comparator_10_lt, comparator_11_eq,
       comparator_12_eq, comparator_13_eq, comparator_14_gt, comparator_15_gt, comparator_16_eq,
       comparator_16_gt, comparator_16_lt, info, main_1_kropka, main_1_out_3, multiplexer_1_out, nand_1_out,
       nand_2_out, nand_3_out, nand_4_out, nie_wyjscie, nor_1_out, not_1_out, not_2_out, not_3_out,
       not_4_out, not_5_out, not_6_out, not_7_out, not_8_out, or_1_out, or_3_out, or_5_out, or_6_out,
       or_7_out, or_9_out, pionek_ruch, pionek_zezwolenie, player_blue, player_green, player_red,
       player_yellow, tunnel, wykryta_kolizja, xor_1_out, xor_2_out, xor_3_out;
  wire [1:0] counter_2_q;
  wire [3:0] main_1_cyfra;
  wire [6:0] adder_1_out, adder_2_out, adder_3_out, adder_4_out, multiplexer_3_out, multiplexer_4_out,
       multiplexer_5_out, multiplexer_6_out, multiplexer_7_out, multiplexer_8_out, subtractor_1_out,
       transistor_7_out;
  wire [12:0] counter_1_q;

  Comparator #(.width(2), .mode("unsigned")) comparator_1 (
    .a(pion_info_odczyt[8:7]), .b(IN_ruch_ktorym_pionem), .eq(comparator_1_eq));  // open: gt, lt
  Comparator #(.width(2), .mode("unsigned")) comparator_2 (
    .a(pion_info_odczyt[10:9]), .b(IN_ktory_gracz), .eq(comparator_2_eq));  // open: gt, lt
  random_generaor_main main_1 (
    .Cyfra(main_1_cyfra), .out_3(main_1_out_3), .Kropka(main_1_kropka), .Losuj(sygnal_losowania), .in_1(in_6));
  Register #(.width(1)) register_1 (.D(main_1_kropka), .Q(out_10), .clk(multiplexer_1_out));  // open: en, clr
  Hex_Digit_Display hex_digit_display_1 (.value(main_1_cyfra));  // open: dp
  and and_1 (pionek_zezwolenie, akceptuj_ruch, comparator_1_eq, comparator_2_eq);
  Comparator #(.width(7)) comparator_3 (
    .a(pion_info_odczyt[6:0]), .b(7'b0001111), .gt(pionek_ruch), .eq(comparator_3_eq), .lt(comparator_3_lt));
  Comparator #(.width(2), .mode("unsigned")) comparator_4 (
    .a(pion_info_odczyt[10:9]), .b(2'b00), .eq(player_red));  // open: gt, lt
  Comparator #(.width(2), .mode("unsigned")) comparator_5 (
    .a(pion_info_odczyt[10:9]), .b(2'b01), .eq(player_blue));  // open: gt, lt
  Comparator #(.width(2), .mode("unsigned")) comparator_6 (
    .a(pion_info_odczyt[10:9]), .b(2'b10), .eq(player_green));  // open: gt, lt
  Comparator #(.width(2), .mode("unsigned")) comparator_7 (
    .a(pion_info_odczyt[10:9]), .b(2'b11), .eq(player_yellow));  // open: gt, lt
  Register #(.width(4)) register_2 (.D(main_1_cyfra), .Q(out_9), .clk(multiplexer_1_out));  // open: en, clr
  Register #(.width(1)) register_3 (.D(main_1_out_3), .Q(info), .clk(multiplexer_1_out));  // open: en, clr
  or or_1 (or_1_out, comparator_3_eq, comparator_3_lt);
  Multiplexer #(.enable("false")) multiplexer_1 (
    .in0(1'b0), .in1(in_6), .out(multiplexer_1_out), .sel(sygnal_losowania));
  nand nand_1 (nand_1_out, out_10, or_1_out, player_red, pionek_zezwolenie);
  nand nand_2 (nand_2_out, out_10, or_1_out, player_blue, pionek_zezwolenie);
  nand nand_3 (nand_3_out, out_10, or_1_out, player_green, pionek_zezwolenie);
  nand nand_4 (nand_4_out, out_10, or_1_out, player_yellow, pionek_zezwolenie);
  not not_1 (not_1_out, out_10);
  Transistor #(.width(7)) transistor_1 (.in(7'b0010000), .out(Pion_Dane_do_zapisu[6:0]), .gate(nand_1_out));
  Transistor #(.width(7)) transistor_2 (.in(7'b0011010), .out(Pion_Dane_do_zapisu[6:0]), .gate(nand_2_out));
  Transistor #(.width(7)) transistor_3 (.in(7'b0100100), .out(Pion_Dane_do_zapisu[6:0]), .gate(nand_3_out));
  nor nor_1 (nor_1_out, nand_1_out, nand_2_out, nand_3_out, nand_4_out);
  xor xor_1 (xor_1_out, nor_1_out, and_9_out);
  xor xor_2 (xor_2_out, xor_1_out, and_12_out);
  xor xor_3 (xor_3_out, xor_2_out, wykryta_kolizja);
  Transistor transistor_4 (.in(pion_info_odczyt[11]), .out(Pion_Dane_do_zapisu[11]), .gate(xor_3_out));
  nand nand_5 (nie_wyjscie, info, not_1_out, or_1_out);
  Transistor #(.width(7)) transistor_5 (.in(7'b0101110), .out(Pion_Dane_do_zapisu[6:0]), .gate(nand_4_out));
  and and_2 (and_2_out, out_10, pionek_zezwolenie, info);
  and and_3 (and_3_out, info, bool_ruch_zapis, pionek_ruch, pionek_zezwolenie);
  Transistor #(.width(7)) transistor_6 (.in(pion_info_odczyt[6:0]), .out(Pion_Dane_do_zapisu[6:0]), .gate(nie_wyjscie));
  Clock clock_1 ();  // open: out
  or or_2 (ZAPISZZ, and_2_out, and_3_out, wykryta_kolizja);
  not not_2 (not_2_out, ZAPISZZ);
  Multiplexer #(.enable("false")) multiplexer_2 (.in0(in_6), .in1(1'b0), .out(CLK_SAVE), .sel(not_2_out));
  and and_4 (and_4_out, info, pionek_ruch, player_red);
  and and_5 (and_5_out, info, pionek_ruch, player_blue);
  and and_6 (and_6_out, info, pionek_ruch, player_green);
  and and_7 (and_7_out, info, pionek_ruch, player_yellow);
  or or_3 (or_3_out, tunnel, and_8_out);
  and and_8 (and_8_out, ZAPISZZ, not_4_out);
  not not_3 (not_3_out, pionek_ruch);
  or or_4 (bool_ruch_zapis, and_4_out, or_5_out);
  Register #(.width(12), .trigger("falling")) register_4 (
    .D({Pion_Dane_do_zapisu[11], pion_info_odczyt[10:7], Pion_Dane_do_zapisu[6:0]}), .Q(podglad),
    .clk(or_3_out), .clr(comparator_13_eq));  // open: en
  not not_4 (not_4_out, wykryta_kolizja);
  Transistor #(.width(7)) transistor_7 (.in({3'b000, out_9}), .out(transistor_7_out), .gate(not_3_out));
  Comparator #(.width(7), .mode("unsigned")) comparator_8 (
    .a(adder_1_out), .b(7'b0110111), .gt(comparator_8_gt));  // open: eq, lt
  Comparator #(.width(7), .mode("unsigned")) comparator_9 (
    .a(pion_info_odczyt[6:0]), .b(7'b0111000), .lt(comparator_9_lt));  // open: gt, eq
  or or_5 (or_5_out, and_5_out, and_6_out, and_7_out);
  or or_6 (or_6_out, and_4_out, or_5_out);
  Adder #(.width(7)) adder_1 (.a(transistor_7_out), .b(pion_info_odczyt[6:0]), .out(adder_1_out));  // open: cin, cout
  and and_9 (and_9_out, comparator_8_gt, comparator_9_lt, or_5_out);
  Comparator #(.width(2), .mode("unsigned")) comparator_10 (
    .a(pion_info_odczyt[10:9]), .b(podglad[10:9]), .gt(comparator_10_gt), .eq(comparator_10_eq),
    .lt(comparator_10_lt));
  Comparator #(.width(7), .mode("unsigned")) comparator_11 (
    .a(podglad[6:0]), .b(pion_info_odczyt[6:0]), .eq(comparator_11_eq));  // open: gt, lt
  and and_10 (and_10_out, wykryta_kolizja, in_6);
  Multiplexer #(.width(7), .enable("false")) multiplexer_3 (
    .in0({7{1'b0}}), .in1(7'b0101000), .out(multiplexer_3_out), .sel(and_9_out));
  Transistor #(.\type ("n")) transistor_8 (.in(1'b1), .out(Pion_Dane_do_zapisu[11]), .gate(and_9_out));
  Comparator #(.width(2)) comparator_12 (
    .a(podglad[8:7]), .b(pion_info_odczyt[8:7]), .eq(comparator_12_eq));  // open: gt, lt
  or or_7 (or_7_out, comparator_10_gt, comparator_10_lt);
  and and_11 (and_11_out, or_7_out, comparator_11_eq);
  Counter #(.width(13), .max('h1fff)) counter_1 (
    .Q(counter_1_q), .clk(and_10_out), .clr(comparator_13_eq));  // open: load, D, count, carry
  Subtractor #(.width(7)) subtractor_1 (
    .a(adder_1_out), .b(multiplexer_3_out), .out(subtractor_1_out));  // open: bin, bout
  not not_5 (not_5_out, comparator_12_eq);
  or or_8 (wykryta_kolizja, and_11_out, and_14_out);
  Comparator #(.width(13), .mode("unsigned")) comparator_13 (
    .a(counter_1_q), .b(13'h2), .eq(comparator_13_eq));  // open: gt, lt
  Multiplexer #(.select(2), .width(7), .enable("false")) multiplexer_4 (
    .in0({7{1'b0}}), .in1(7'b0011001), .in2(7'b0100011), .in3(7'b0101101), .out(multiplexer_4_out),
    .sel(pion_info_odczyt[10:9]));
  Multiplexer #(.select(2), .width(7), .enable("false")) multiplexer_5 (
    .in0({7{1'b0}}), .in1(7'b0100010), .in2(7'b0011100), .in3(7'b0011001), .out(multiplexer_5_out),
    .sel(pion_info_odczyt[10:9]));
  Comparator #(.width(7), .mode("unsigned")) comparator_14 (
    .a(adder_1_out), .b(multiplexer_4_out), .gt(comparator_14_gt));  // open: eq, lt
  Comparator #(.width(7), .mode("unsigned")) comparator_15 (
    .a(pion_info_odczyt[6:0]), .b(7'b0001111), .gt(comparator_15_gt));  // open: eq, lt
  Multiplexer #(.select(2), .width(7), .enable("false")) multiplexer_6 (
    .in0({7{1'b0}}), .in1(7'b0000100), .in2(7'b0001000), .in3(7'b0001100), .out(multiplexer_6_out),
    .sel(pion_info_odczyt[10:9]));
  Multiplexer #(.width(7), .enable("false")) multiplexer_7 (
    .in0({7{1'b0}}), .in1(multiplexer_5_out), .out(multiplexer_7_out), .sel(and_12_out));
  and and_12 (and_12_out, pion_info_odczyt[11], comparator_14_gt);
  and and_13 (and_13_out, and_12_out, not_7_out);
  and and_14 (and_14_out, not_5_out, comparator_11_eq, comparator_10_eq, comparator_15_gt);
  not not_6 (not_6_out, and_11_out);
  Adder #(.width(7)) adder_2 (
    .a(multiplexer_6_out), .b({{5{1'b0}}, pion_info_odczyt[8:7]}), .out(adder_2_out));  // open: cin, cout
  Adder #(.width(7)) adder_3 (.a(subtractor_1_out), .b(multiplexer_7_out), .out(adder_3_out));  // open: cin, cout
  not not_7 (not_7_out, and_17_out);
  Transistor #(.\type ("n")) transistor_9 (.in(1'b0), .out(Pion_Dane_do_zapisu[11]), .gate(and_13_out));
  Transistor #(.width(7)) transistor_10 (.in(adder_2_out), .out(Pion_Dane_do_zapisu[6:0]), .gate(not_6_out));
  Multiplexer #(.select(2), .width(7), .enable("false")) multiplexer_8 (
    .in0(7'b0111011), .in1(7'b0111111), .in2(7'b1000011), .in3(7'b1000111), .out(multiplexer_8_out),
    .sel(pion_info_odczyt[10:9]));
  assign Pion_Dane_do_zapisu[6:0] = and_14_out ? adder_4_out : 7'bz;  // Controlled_Buffer controlled_buffer_1
  Adder #(.width(7)) adder_4 (.a(pion_info_odczyt[6:0]), .b(7'b0000001), .out(adder_4_out));  // open: cin, cout
  Transistor #(.\type ("n"), .gate("br"), .width(7)) transistor_11 (
    .in(adder_3_out), .out(Pion_Dane_do_zapisu[6:0]), .gate(and_15_out));
  and and_15 (and_15_out, or_6_out, not_8_out, or_9_out);
  or or_9 (or_9_out, comparator_16_eq, comparator_16_lt);
  Comparator #(.width(7), .mode("unsigned")) comparator_16 (
    .a(adder_3_out), .b(multiplexer_8_out), .gt(comparator_16_gt), .eq(comparator_16_eq),
    .lt(comparator_16_lt));
  Counter #(.width(2), .max('h3)) counter_2 (
    .Q(counter_2_q), .clk(and_16_out), .clr(tunnel));  // open: load, D, count, carry
  and and_16 (and_16_out, and_14_out, in_6);
  Transistor transistor_12 (.in(1'b0), .out(Pion_Dane_do_zapisu[11]), .gate(not_6_out));
  not not_8 (not_8_out, wykryta_kolizja);
  and and_17 (and_17_out, or_6_out, not_8_out, comparator_16_gt);
  and and_18 (and_18_out, and_17_out, pion_info_odczyt[11]);
  Transistor #(.\type ("n")) transistor_13 (
    .in(pion_info_odczyt[11]), .out(Pion_Dane_do_zapisu[11]), .gate(and_18_out));
  Comparator #(.width(2), .mode("unsigned")) comparator_17 (.a(counter_2_q), .b(2'b11), .eq(tunnel));  // open: gt, lt
  Transistor #(.\type ("n")) transistor_14 (.in(1'b0), .out(Pion_Dane_do_zapisu[11]), .gate(and_14_out));
  Transistor #(.\type ("n"), .width(7)) transistor_15 (
    .in(pion_info_odczyt[6:0]), .out(Pion_Dane_do_zapisu[6:0]), .gate(and_17_out));

  assign Pion_Dane_do_zapisu[10:7] = pion_info_odczyt[10:7];

  // Other names for the same wires on the sheet: nr_pionka[1:0] = pion_info_odczyt[8:7]; CLK = in_6; dot = out_10;
  //   stan_pion[6:0] = Pion_Dane_do_zapisu[6:0]; kolor[1:0] = pion_info_odczyt[10:9];
  //   Flaga_zapis = Pion_Dane_do_zapisu[11]; Pozycja[6:0] = pion_info_odczyt[6:0]; Flaga = pion_info_odczyt[11];
  //   nr_pionka_kol[1:0] = podglad[8:7]; rzut_liczba[3:0] = out_9; zapisz = ZAPISZZ

  // Notes on the sheet:
  //   Czerwony
  //   Niebieskiego
  //   Zielony
  //   Zółty
  //   Warunek czy pion jest na polu startowym
  //   #1 Wyjscie z bazy
  //   Warunki logiczne
  //   Zezwolenia na zapis
  //   Force'owanie przerzucenia na pole start
  //   sterowanie logiczne
  //   #2 poruszanie się po planszy
  //   sprawdz czy wszedl do bazy
  //   Bugfix zapisu przy kolizji
  //   Delay resetu przy kolizji
  //   #3 Handle exceptions
  //   Dodaj zeby wszedl do bazy
  //   RESET PION
  //   KOLIZJA Z INNYM GRACZEM
  //   #4 wejście do bazy
  //   Dorzucamy zmienna w pionku ktora bedzie mowic czy przeszla juz przez punkt przegiecia
  //   Potem juz latwiej sterowac logika przy bazie
  //   Zatrzymanie maks pole
  //   KOLIZJA Z WŁASNYM PIONKIEM
  //   Po kolizji reset zmiennej "przegiecia"
endmodule
