// Logisim project projekt.circ as structural Verilog: 1 circuit, main circuit main
module main (
  input  [1:0] wybierz_pionka,
  input  in_2,
  output Klikaj
);

  wire demultiplexer_1_out0, demultiplexer_1_out1, demultiplexer_1_out2, demultiplexer_1_out3,
       \kulnij_kostką_out , led_4_p3, led_4_p4, Rusz_out, zakoncz_ture_out;
  wire [1:0] main_1_mux_kolor_outside;
  wire [3:0] main_1_liczba;
  wire [4:4] main_1_liczba_2;
  wire [6:0] main_1_x, main_1_y;
  wire [15:0] main_1_rgb;

  Demultiplexer #(.select(2), .enable("false")) demultiplexer_1 (
    .out0(demultiplexer_1_out0), .out1(demultiplexer_1_out1), .out2(demultiplexer_1_out2),
    .out3(demultiplexer_1_out3), .in(1'b1), .sel(main_1_mux_kolor_outside));
  Button \kulnij_kostką  (.out(\kulnij_kostką_out ));
  Button Rusz (.out(Rusz_out));
  Button zakoncz_ture (.out(zakoncz_ture_out));
  Hex_Digit_Display hex_digit_display_1 (.value(main_1_liczba), .dp(main_1_liczba_2[4]));
  // LED led_1: pin names not known; wires that end beside it: demultiplexer_1_out0
  // LED led_2: pin names not known; wires that end beside it: demultiplexer_1_out1
  // LED led_3: pin names not known; wires that end beside it: demultiplexer_1_out2
  // LED led_4: pin names not known; wires that end beside it: in_2, demultiplexer_1_out3, led_4_p3, led_4_p4, 1'b1
  Button button_1 (.out(led_4_p3));
  Clock clock_1 (.out(led_4_p4));
  chinczyk_game_main main_1 (
    .nr_pionka(wybierz_pionka), .X(main_1_x), .losuj(\kulnij_kostką_out ), .RGB(main_1_rgb),
    .mux_kolor_outside(main_1_mux_kolor_outside), .Y(main_1_y), .mozesz_losowac(Klikaj),
    .liczba({main_1_liczba_2[4], main_1_liczba}), .zakoncz_ture(zakoncz_ture_out), .mozesz_ruszyc(Rusz_out));  // open: in_1
  // LCD_Video lcd_video_1: pin names not known; wires that end beside it: main_1_x, main_1_y, main_1_rgb

  // Notes on the sheet:
  //   ROZPOCZNIJ
  //   CTRL + K (zalecana częstotliwość conajmniej 2k)
  //   -rozpocznij symulacje
  //   Jak grac?
  //   -kliknij "kulnij_kostką'' aby wylosować liczbe
  //   -zmien wartosc "wybierz pionka" aby wybrac
  //   ktorym pionkiem poruszyć, 00 - 1; 01 - 1; 10 -2 ; 11 - 3 
  //   -kliknij "rusz" aby ruszyc wybranym pionkiem
  //   -ruch wykona sie, w momencie gdy "klikaj" ma 1
  //   -po skonczeniu tury klikamy "zakoncz_ture"
  //   Zasady
  //   -gracze mogą zbijać pionki innych graczy
  //   -pola wyjscia są bezpieczne i nie mozna na nich zbijac
  //   Zalecane Zasady
  //   -jezeli gracz wykulnie 6, moze kulnac jeszcze raz (max 3)
  //   -wygrywa gracz, ktory wejdzie wszystkimi pionkami do bazy
  //   -wejscie na wlasnego pionka, powoduje odbicie go o 1 pole do przodu
  //   -gdy jeden z graczy wygra, gre mozna kontynuować, turę wygranego można pomijać
  //   Autorzy
  //   Rafał Szygenda
  //   Jacek Szwed
  //   Jakub Szymczak
endmodule
